// Digital circuit CPU_RISCV.dig as structural Verilog
module CPU_RISCV (
  input  Clock,
  input  Reset,
  input  EX_MEM_Flush,
  input  MEM_WB_Flush,
  input  Enable,
  input  LoadWrite_DM,
  input  [31:0] LoadAddress_DM,
  input  [31:0] LoadData_DM,
  input  LoadWrite_IM,
  input  [31:0] LoadAddress_IM,
  input  [31:0] LoadData_IM,
  output [31:0] Result,
  output Zero,
  output [31:0] PC,
  output [31:0] PCPlus4,
  output [31:0] Instruction,
  output [31:0] IF_ID_PC,
  output [31:0] IF_ID_Instruction,
  output [6:0] ID_opcode,
  output [4:0] ID_rd,
  output [4:0] ID_rs1,
  output [4:0] ID_rs2,
  output [2:0] ID_funct3,
  output [6:0] ID_funct7,
  output [31:0] ID_Immediate,
  output [3:0] ID_ALUControl,
  output [31:0] MEM_ALUResult,
  output [31:0] WB_ALUResult,
  output [31:0] RF_ReadData1,
  output [31:0] RF_ReadData2,
  output [31:0] DebugX3,
  output [31:0] DebugX4,
  output [31:0] DebugALU_A,
  output [31:0] DebugX1,
  output [31:0] ReadData,
  output [31:0] DebugX2
);

  wire or_1_out, or_2_out, or_3_out, u_BranchJumpUnit_32_takebranch, u_ControlUnit_32_alusrc,
       u_ControlUnit_32_branch, u_ControlUnit_32_jump, u_ControlUnit_32_memread, u_ControlUnit_32_memtoreg,
       u_ControlUnit_32_memwrite, u_ControlUnit_32_regwrite, u_EX_MEM_Register_jump_out,
       u_EX_MEM_Register_memread_out, u_EX_MEM_Register_memtoreg_out, u_EX_MEM_Register_memwrite_out,
       u_EX_MEM_Register_regwrite_out, u_HazardDetectionUnit_32_id_ex_flush,
       u_HazardDetectionUnit_32_if_id_write, u_HazardDetectionUnit_32_pcwrite, u_ID_EX_Register_alusrc_out,
       u_ID_EX_Register_branch_out, u_ID_EX_Register_jump_out, u_ID_EX_Register_memread_out,
       u_ID_EX_Register_memtoreg_out, u_ID_EX_Register_memwrite_out, u_ID_EX_Register_regwrite_out,
       u_InstructionDecoder_32_usesrs1, u_InstructionDecoder_32_usesrs2, u_MEM_WB_Register_jump_out,
       u_MEM_WB_Register_memtoreg_out, u_MEM_WB_Register_regwrite_out;
  wire [1:0] u_ControlUnit_32_aluop, u_ForwardingUnit_32_forwarda, u_ForwardingUnit_32_forwardb,
       u_ID_EX_Register_aluop_out;
  wire [2:0] u_ID_EX_Register_funct3_out;
  wire [4:0] u_EX_MEM_Register_rd_out, u_ID_EX_Register_rd_out, u_ID_EX_Register_rs1_out,
       u_ID_EX_Register_rs2_out, u_MEM_WB_Register_rd_out;
  wire [6:0] u_ID_EX_Register_funct7_out, u_ID_EX_Register_opcode_out;
  wire [31:0] u_ALUSrcMux_32_alub, u_BranchJumpUnit_32_targetpc, u_DataMemory_32_debugloaddata,
       u_EX_MEM_Register_pc_out, u_EX_MEM_Register_writedata_out, u_ForwardAMux_32_result,
       u_ForwardBMux_32_result, u_ID_EX_Register_immediate_out, u_ID_EX_Register_pc_out,
       u_ID_EX_Register_readdata1_out, u_ID_EX_Register_readdata2_out, u_InstructionMemory_32_debugloaddata,
       u_MEM_WB_Register_pc_out, u_MEM_WB_Register_readdata_out, u_NextPCMux_32_nextpc,
       u_WriteBackMux_32_writebackdata;

  ForwardBMux_32 #(.applicationType("IVERILOG"), .CodeFile("/Users/kellysoares/Documents/Faculdade/arqComp/RICV_entrega/ForwardBMux_32.v")) u_ForwardBMux_32 (
    .OriginalData(u_ID_EX_Register_readdata2_out), .EX_MEM_Data(MEM_ALUResult),
    .MEM_WB_Data(u_WriteBackMux_32_writebackdata), .ForwardB(u_ForwardingUnit_32_forwardb),
    .Result(u_ForwardBMux_32_result));
  ForwardAMux_32 #(.applicationType("IVERILOG"), .CodeFile("/Users/kellysoares/Documents/Faculdade/arqComp/RICV_entrega/ForwardAMux_32.v")) u_ForwardAMux_32 (
    .OriginalData(u_ID_EX_Register_readdata1_out), .EX_MEM_Data(MEM_ALUResult),
    .MEM_WB_Data(u_WriteBackMux_32_writebackdata), .ForwardA(u_ForwardingUnit_32_forwarda),
    .Result(u_ForwardAMux_32_result));
  or or_1 (or_1_out, u_BranchJumpUnit_32_takebranch, u_HazardDetectionUnit_32_id_ex_flush);
  BranchJumpUnit_32 #(.applicationType("IVERILOG"), .CodeFile("/Users/kellysoares/Documents/Faculdade/arqComp/RICV_entrega/BranchJumpUnit_32.v")) u_BranchJumpUnit_32 (
    .PC(u_ID_EX_Register_pc_out), .ReadData1(u_ForwardAMux_32_result), .ReadData2(u_ForwardBMux_32_result),
    .Immediate(u_ID_EX_Register_immediate_out), .opcode(u_ID_EX_Register_opcode_out),
    .funct3(u_ID_EX_Register_funct3_out), .TargetPC(u_BranchJumpUnit_32_targetpc),
    .TakeBranch(u_BranchJumpUnit_32_takebranch));
  or or_2 (or_2_out, u_BranchJumpUnit_32_takebranch, u_HazardDetectionUnit_32_pcwrite);
  NextPCMux_32 #(.applicationType("IVERILOG"), .CodeFile("/Users/kellysoares/Documents/Faculdade/arqComp/RICV_entrega/NextPCMux_32.v")) u_NextPCMux_32 (
    .PCPlus4(PCPlus4), .TargetPC(u_BranchJumpUnit_32_targetpc), .TakeBranch(u_BranchJumpUnit_32_takebranch),
    .NextPC(u_NextPCMux_32_nextpc));
  ProgramCounter_32 #(.applicationType("IVERILOG"), .CodeFile("/Users/kellysoares/Documents/Faculdade/arqComp/RICV_entrega/ProgramCounter_32.v")) u_ProgramCounter_32 (
    .clk(Clock), .reset(Reset), .PCWrite(or_2_out), .NextPC(u_NextPCMux_32_nextpc), .Enable(Enable), .PC(PC));
  RegisterFile_32 #(.applicationType("IVERILOG"), .CodeFile("/Users/kellysoares/Documents/Faculdade/arqComp/RICV_entrega/RegisterFile_32.v")) u_RegisterFile_32 (
    .clk(Clock), .reset(Reset), .RegWrite(u_MEM_WB_Register_regwrite_out), .rs1(ID_rs1), .rs2(ID_rs2),
    .rd(u_MEM_WB_Register_rd_out), .WriteData(u_WriteBackMux_32_writebackdata), .Enable(Enable),
    .ReadData1(RF_ReadData1), .ReadData2(RF_ReadData2), .DebugX3(DebugX3), .DebugX4(DebugX4),
    .DebugX1(DebugX1), .DebugX2(DebugX2));
  ALUSrcMux_32 #(.applicationType("IVERILOG"), .CodeFile("/Users/kellysoares/Documents/Faculdade/arqComp/RICV_entrega/ALUSrcMux_32.v")) u_ALUSrcMux_32 (
    .ReadData2(u_ForwardBMux_32_result), .Immediate(u_ID_EX_Register_immediate_out),
    .ALUSrc(u_ID_EX_Register_alusrc_out), .ALUB(u_ALUSrcMux_32_alub));
  ALUInputAMux_32 #(.applicationType("IVERILOG"), .CodeFile("/Users/kellysoares/Documents/Faculdade/arqComp/RICV_entrega/ALUInputAMux_32.v")) u_ALUInputAMux_32 (
    .ForwardedData(u_ForwardAMux_32_result), .PC(u_ID_EX_Register_pc_out),
    .opcode(u_ID_EX_Register_opcode_out), .Result(DebugALU_A));
  ALU_32 #(.applicationType("IVERILOG"), .CodeFile("/Users/kellysoares/Documents/Faculdade/arqComp/RICV_entrega/ALU_32.v")) u_ALU_32 (
    .A(DebugALU_A), .B(u_ALUSrcMux_32_alub), .ALUControl(ID_ALUControl), .Result(Result), .Zero(Zero));
  ID_EX_Register #(.applicationType("IVERILOG"), .CodeFile("/Users/kellysoares/Documents/Faculdade/arqComp/RICV_entrega/ID_EX_Register.v")) u_ID_EX_Register (
    .clk(Clock), .reset(Reset), .Flush(or_1_out), .PC_in(IF_ID_PC), .ReadData1_in(RF_ReadData1),
    .ReadData2_in(RF_ReadData2), .Immediate_in(ID_Immediate), .rs1_in(ID_rs1), .rs2_in(ID_rs2),
    .rd_in(ID_rd), .Enable(Enable), .ALUSrc_in(u_ControlUnit_32_alusrc),
    .RegWrite_in(u_ControlUnit_32_regwrite), .MemRead_in(u_ControlUnit_32_memread),
    .MemWrite_in(u_ControlUnit_32_memwrite), .MemToReg_in(u_ControlUnit_32_memtoreg),
    .Branch_in(u_ControlUnit_32_branch), .Jump_in(u_ControlUnit_32_jump), .opcode_in(ID_opcode),
    .funct3_in(ID_funct3), .funct7_in(ID_funct7), .ALUOp_in(u_ControlUnit_32_aluop),
    .PC_out(u_ID_EX_Register_pc_out), .ReadData1_out(u_ID_EX_Register_readdata1_out),
    .ReadData2_out(u_ID_EX_Register_readdata2_out), .Immediate_out(u_ID_EX_Register_immediate_out),
    .rs1_out(u_ID_EX_Register_rs1_out), .rs2_out(u_ID_EX_Register_rs2_out), .rd_out(u_ID_EX_Register_rd_out),
    .ALUSrc_out(u_ID_EX_Register_alusrc_out), .RegWrite_out(u_ID_EX_Register_regwrite_out),
    .MemRead_out(u_ID_EX_Register_memread_out), .MemWrite_out(u_ID_EX_Register_memwrite_out),
    .MemToReg_out(u_ID_EX_Register_memtoreg_out), .Branch_out(u_ID_EX_Register_branch_out),
    .Jump_out(u_ID_EX_Register_jump_out), .opcode_out(u_ID_EX_Register_opcode_out),
    .funct3_out(u_ID_EX_Register_funct3_out), .funct7_out(u_ID_EX_Register_funct7_out),
    .ALUOp_out(u_ID_EX_Register_aluop_out));  // open: ALUControl_out
  or or_3 (or_3_out, u_HazardDetectionUnit_32_if_id_write, u_BranchJumpUnit_32_takebranch);
  IF_ID_Register #(.applicationType("IVERILOG"), .CodeFile("/Users/kellysoares/Documents/Faculdade/arqComp/RICV_entrega/IF_ID_Register.v")) u_IF_ID_Register (
    .clk(Clock), .reset(Reset), .IF_ID_Write(or_3_out), .Flush(u_BranchJumpUnit_32_takebranch), .PC_in(PC),
    .Instruction_in(Instruction), .Enable(Enable), .PC_out(IF_ID_PC), .Instruction_out(IF_ID_Instruction));
  InstructionMemory_32 #(.applicationType("IVERILOG"), .CodeFile("/Users/kellysoares/Documents/Faculdade/arqComp/RICV_entrega/InstructionMemory_32.v")) u_InstructionMemory_32 (
    .Address(PC), .Enable(Enable), .LoadWrite(LoadWrite_IM), .LoadAddress(LoadAddress_IM),
    .LoadData(LoadData_IM), .Instruction(Instruction), .DebugLoadData(u_InstructionMemory_32_debugloaddata));
  PC_Adder_32 #(.applicationType("IVERILOG"), .CodeFile("/Users/kellysoares/Documents/Faculdade/arqComp/RICV_entrega/PC_Adder_32.v")) u_PC_Adder_32 (
    .PC(PC), .PCPlus4(PCPlus4));
  ForwardingUnit_32 #(.applicationType("IVERILOG"), .CodeFile("/Users/kellysoares/Documents/Faculdade/arqComp/RICV_entrega/ForwardingUnit_32.v")) u_ForwardingUnit_32 (
    .ID_EX_rs1(u_ID_EX_Register_rs1_out), .ID_EX_rs2(u_ID_EX_Register_rs2_out),
    .EX_MEM_rd(u_EX_MEM_Register_rd_out), .EX_MEM_RegWrite(u_EX_MEM_Register_regwrite_out),
    .EX_MEM_MemToReg(u_EX_MEM_Register_memtoreg_out), .MEM_WB_rd(u_MEM_WB_Register_rd_out),
    .MEM_WB_RegWrite(u_MEM_WB_Register_regwrite_out), .ForwardA(u_ForwardingUnit_32_forwarda),
    .ForwardB(u_ForwardingUnit_32_forwardb));
  // Probe on u_InstructionMemory_32_debugloaddata
  EX_MEM_Register #(.applicationType("IVERILOG"), .CodeFile("/Users/kellysoares/Documents/Faculdade/arqComp/RICV_entrega/EX_MEM_Register.v")) u_EX_MEM_Register (
    .clk(Clock), .reset(Reset), .Flush(EX_MEM_Flush), .PC_in(u_ID_EX_Register_pc_out), .ALUResult_in(Result),
    .WriteData_in(u_ForwardBMux_32_result), .rd_in(u_ID_EX_Register_rd_out), .Zero_in(Zero),
    .RegWrite_in(u_ID_EX_Register_regwrite_out), .MemRead_in(u_ID_EX_Register_memread_out),
    .MemWrite_in(u_ID_EX_Register_memwrite_out), .MemToReg_in(u_ID_EX_Register_memtoreg_out),
    .Branch_in(u_ID_EX_Register_branch_out), .Jump_in(u_ID_EX_Register_jump_out), .Enable(Enable),
    .PC_out(u_EX_MEM_Register_pc_out), .ALUResult_out(MEM_ALUResult),
    .WriteData_out(u_EX_MEM_Register_writedata_out), .rd_out(u_EX_MEM_Register_rd_out),
    .RegWrite_out(u_EX_MEM_Register_regwrite_out), .MemRead_out(u_EX_MEM_Register_memread_out),
    .MemWrite_out(u_EX_MEM_Register_memwrite_out), .MemToReg_out(u_EX_MEM_Register_memtoreg_out),
    .Jump_out(u_EX_MEM_Register_jump_out));  // open: Zero_out, Branch_out
  HazardDetectionUnit_32 #(.applicationType("IVERILOG"), .CodeFile("/Users/kellysoares/Documents/Faculdade/arqComp/RICV_entrega/HazardDetectionUnit_32.v")) u_HazardDetectionUnit_32 (
    .ID_EX_rd(u_ID_EX_Register_rd_out), .ID_EX_MemRead(u_ID_EX_Register_memread_out), .IF_ID_rs1(ID_rs1),
    .IF_ID_rs2(ID_rs2), .IF_ID_UsesRs1(u_InstructionDecoder_32_usesrs1),
    .IF_ID_UsesRs2(u_InstructionDecoder_32_usesrs2), .PCWrite(u_HazardDetectionUnit_32_pcwrite),
    .IF_ID_Write(u_HazardDetectionUnit_32_if_id_write), .ID_EX_Flush(u_HazardDetectionUnit_32_id_ex_flush));
  InstructionDecoder_32 #(.applicationType("IVERILOG"), .CodeFile("/Users/kellysoares/Documents/Faculdade/arqComp/RICV_entrega/InstructionDecoder_32.v")) u_InstructionDecoder_32 (
    .Instruction(IF_ID_Instruction), .opcode(ID_opcode), .rs1(ID_rs1), .rs2(ID_rs2), .rd(ID_rd),
    .funct3(ID_funct3), .funct7(ID_funct7), .UsesRs1(u_InstructionDecoder_32_usesrs1),
    .UsesRs2(u_InstructionDecoder_32_usesrs2));
  ImmediateGenerator_32 #(.applicationType("IVERILOG"), .CodeFile("/Users/kellysoares/Documents/Faculdade/arqComp/RICV_entrega/ImmediateGenerator_32.v")) u_ImmediateGenerator_32 (
    .Instruction(IF_ID_Instruction), .Immediate(ID_Immediate));
  MEM_WB_Register #(.applicationType("IVERILOG"), .CodeFile("/Users/kellysoares/Documents/Faculdade/arqComp/RICV_entrega/MEM_WB_Register.v")) u_MEM_WB_Register (
    .clk(Clock), .reset(Reset), .Flush(MEM_WB_Flush), .ALUResult_in(MEM_ALUResult), .ReadData_in(ReadData),
    .rd_in(u_EX_MEM_Register_rd_out), .RegWrite_in(u_EX_MEM_Register_regwrite_out),
    .MemToReg_in(u_EX_MEM_Register_memtoreg_out), .PC_in(u_EX_MEM_Register_pc_out),
    .Jump_in(u_EX_MEM_Register_jump_out), .Enable(Enable), .ALUResult_out(WB_ALUResult),
    .ReadData_out(u_MEM_WB_Register_readdata_out), .rd_out(u_MEM_WB_Register_rd_out),
    .RegWrite_out(u_MEM_WB_Register_regwrite_out), .MemToReg_out(u_MEM_WB_Register_memtoreg_out),
    .PC_out(u_MEM_WB_Register_pc_out), .Jump_out(u_MEM_WB_Register_jump_out));
  ControlUnit_32 #(.applicationType("IVERILOG"), .CodeFile("/Users/kellysoares/Documents/Faculdade/arqComp/RICV_entrega/ControlUnit_32.v")) u_ControlUnit_32 (
    .opcode(ID_opcode), .RegWrite(u_ControlUnit_32_regwrite), .ALUSrc(u_ControlUnit_32_alusrc),
    .MemRead(u_ControlUnit_32_memread), .MemWrite(u_ControlUnit_32_memwrite),
    .MemToReg(u_ControlUnit_32_memtoreg), .Branch(u_ControlUnit_32_branch), .Jump(u_ControlUnit_32_jump),
    .ALUOp(u_ControlUnit_32_aluop));
  DataMemory_32 #(.applicationType("IVERILOG"), .CodeFile("/Users/kellysoares/Documents/Faculdade/arqComp/RICV_entrega/DataMemory_32.v")) u_DataMemory_32 (
    .clk(Clock), .reset(Reset), .MemRead(u_EX_MEM_Register_memread_out),
    .MemWrite(u_EX_MEM_Register_memwrite_out), .Address(MEM_ALUResult),
    .WriteData(u_EX_MEM_Register_writedata_out), .Enable(Enable), .LoadWrite(LoadWrite_DM),
    .LoadAddress(LoadAddress_DM), .LoadData(LoadData_DM), .ReadData(ReadData),
    .DebugLoadData(u_DataMemory_32_debugloaddata));
  ALUControl_32 #(.applicationType("IVERILOG"), .CodeFile("/Users/kellysoares/Documents/Faculdade/arqComp/RICV_entrega/ALUControl_32.v")) u_ALUControl_32 (
    .ALUOp(u_ID_EX_Register_aluop_out), .opcode(u_ID_EX_Register_opcode_out),
    .funct3(u_ID_EX_Register_funct3_out), .funct7(u_ID_EX_Register_funct7_out), .ALUControl(ID_ALUControl));
  WriteBackMux_32 #(.applicationType("IVERILOG"), .CodeFile("/Users/kellysoares/Documents/Faculdade/arqComp/RICV_entrega/WriteBackMux_32.v")) u_WriteBackMux_32 (
    .ALUResult(WB_ALUResult), .ReadData(u_MEM_WB_Register_readdata_out),
    .MemToReg(u_MEM_WB_Register_memtoreg_out), .PC(u_MEM_WB_Register_pc_out),
    .Jump(u_MEM_WB_Register_jump_out), .WriteBackData(u_WriteBackMux_32_writebackdata));
  // Probe on u_DataMemory_32_debugloaddata
endmodule
