// Digital circuit teste_MEM_WB_Register.dig as structural Verilog
module teste_MEM_WB_Register (
  input  clk,
  input  reset,
  input  RegWrite,
  input  [4:0] rs1,
  input  [4:0] rs2,
  input  [4:0] rd,
  input  [31:0] WriteData,
  input  PCWrite,
  input  IF_ID_Write,
  input  Flush,
  input  ID_EX_Flush,
  input  EX_MEM_Flush,
  input  MEM_WB_Flush,
  input  [31:0] MEM_ReadData_Temp,
  output [31:0] Result,
  output Zero,
  output [31:0] PC,
  output [31:0] PCPlus4,
  output [31:0] Instruction,
  output [31:0] IF_ID_PC,
  output [31:0] IF_ID_Instruction,
  output [6:0] ID_opcode,
  output [4:0] ID_rd,
  output [4:0] ID_rs1,
  output [4:0] ID_rs2,
  output [2:0] ID_funct3,
  output [6:0] ID_funct7,
  output [31:0] ID_Immediate,
  output ID_RegWrite,
  output ID_ALUSrc,
  output ID_MemRead,
  output ID_MemWrite,
  output ID_MemToReg,
  output ID_Branch,
  output ID_Jump,
  output [1:0] ID_ALUOp,
  output [3:0] ID_ALUControl,
  output [31:0] MEM_ALUResult,
  output [31:0] WB_ALUResult
);

  wire u_EX_MEM_Register_memtoreg_out, u_EX_MEM_Register_regwrite_out, u_ID_EX_Register_alusrc_out,
       u_ID_EX_Register_branch_out, u_ID_EX_Register_jump_out, u_ID_EX_Register_memread_out,
       u_ID_EX_Register_memtoreg_out, u_ID_EX_Register_memwrite_out, u_ID_EX_Register_regwrite_out;
  wire [3:0] u_ID_EX_Register_alucontrol_out;
  wire [4:0] u_EX_MEM_Register_rd_out, u_ID_EX_Register_rd_out;
  wire [31:0] u_ALUSrcMux_32_alub, u_ID_EX_Register_immediate_out, u_ID_EX_Register_pc_out,
       u_ID_EX_Register_readdata1_out, u_ID_EX_Register_readdata2_out, u_RegisterFile_32_readdata1,
       u_RegisterFile_32_readdata2;

  ProgramCounter_32 #(.applicationType("IVERILOG"), .CodeFile("/Users/kellysoares/Documents/Faculdade/arqComp/RICV_entrega/ProgramCounter_32.v")) u_ProgramCounter_32 (
    .clk(clk), .reset(reset), .PCWrite(PCWrite), .NextPC(PCPlus4), .PC(PC));
  RegisterFile_32 #(.applicationType("IVERILOG"), .CodeFile("/Users/kellysoares/Documents/Faculdade/arqComp/RICV_entrega/RegisterFile_32.v")) u_RegisterFile_32 (
    .clk(clk), .reset(reset), .RegWrite(RegWrite), .rs1(rs1), .rs2(rs2), .rd(rd), .WriteData(WriteData),
    .ReadData1(u_RegisterFile_32_readdata1), .ReadData2(u_RegisterFile_32_readdata2));
  ALUSrcMux_32 #(.applicationType("IVERILOG"), .CodeFile("/Users/kellysoares/Documents/Faculdade/arqComp/RICV_entrega/ALUSrcMux_32.v")) u_ALUSrcMux_32 (
    .ReadData2(u_ID_EX_Register_readdata2_out), .Immediate(u_ID_EX_Register_immediate_out),
    .ALUSrc(u_ID_EX_Register_alusrc_out), .ALUB(u_ALUSrcMux_32_alub));
  InstructionMemory_32 #(.applicationType("IVERILOG"), .CodeFile("/Users/kellysoares/Documents/Faculdade/arqComp/RICV_entrega/InstructionMemory_32.v")) u_InstructionMemory_32 (
    .Address(PC), .Instruction(Instruction));
  PC_Adder_32 #(.applicationType("IVERILOG"), .CodeFile("/Users/kellysoares/Documents/Faculdade/arqComp/RICV_entrega/PC_Adder_32.v")) u_PC_Adder_32 (
    .PC(PC), .PCPlus4(PCPlus4));
  ALU_32 #(.applicationType("IVERILOG"), .CodeFile("/Users/kellysoares/Documents/Faculdade/arqComp/RICV_entrega/ALU_32.v")) u_ALU_32 (
    .A(u_ID_EX_Register_readdata1_out), .B(u_ALUSrcMux_32_alub),
    .ALUControl(u_ID_EX_Register_alucontrol_out), .Result(Result), .Zero(Zero));
  ID_EX_Register #(.applicationType("IVERILOG"), .CodeFile("/Users/kellysoares/Documents/Faculdade/arqComp/RICV_entrega/ID_EX_Register.v")) u_ID_EX_Register (
    .clk(clk), .reset(reset), .Flush(ID_EX_Flush), .PC_in(IF_ID_PC),
    .ReadData1_in(u_RegisterFile_32_readdata1), .ReadData2_in(u_RegisterFile_32_readdata2),
    .Immediate_in(ID_Immediate), .rs1_in(ID_rs1), .rs2_in(ID_rs2), .rd_in(ID_rd),
    .ALUControl_in(ID_ALUControl), .ALUSrc_in(ID_ALUSrc), .RegWrite_in(ID_RegWrite), .MemRead_in(ID_MemRead),
    .MemWrite_in(ID_MemWrite), .MemToReg_in(ID_MemToReg), .Branch_in(ID_Branch), .Jump_in(ID_Jump),
    .PC_out(u_ID_EX_Register_pc_out), .ReadData1_out(u_ID_EX_Register_readdata1_out),
    .ReadData2_out(u_ID_EX_Register_readdata2_out), .Immediate_out(u_ID_EX_Register_immediate_out),
    .rd_out(u_ID_EX_Register_rd_out), .ALUControl_out(u_ID_EX_Register_alucontrol_out),
    .ALUSrc_out(u_ID_EX_Register_alusrc_out), .RegWrite_out(u_ID_EX_Register_regwrite_out),
    .MemRead_out(u_ID_EX_Register_memread_out), .MemWrite_out(u_ID_EX_Register_memwrite_out),
    .MemToReg_out(u_ID_EX_Register_memtoreg_out), .Branch_out(u_ID_EX_Register_branch_out),
    .Jump_out(u_ID_EX_Register_jump_out));  // open: rs1_out, rs2_out
  IF_ID_Register #(.applicationType("IVERILOG"), .CodeFile("/Users/kellysoares/Documents/Faculdade/arqComp/RICV_entrega/IF_ID_Register.v")) u_IF_ID_Register (
    .clk(clk), .reset(reset), .IF_ID_Write(IF_ID_Write), .Flush(Flush), .PC_in(PC),
    .Instruction_in(Instruction), .PC_out(IF_ID_PC), .Instruction_out(IF_ID_Instruction));
  EX_MEM_Register #(.applicationType("IVERILOG"), .CodeFile("/Users/kellysoares/Documents/Faculdade/arqComp/RICV_entrega/EX_MEM_Register.v")) u_EX_MEM_Register (
    .clk(clk), .reset(reset), .Flush(EX_MEM_Flush), .PC_in(u_ID_EX_Register_pc_out), .ALUResult_in(Result),
    .WriteData_in(u_ID_EX_Register_readdata2_out), .rd_in(u_ID_EX_Register_rd_out), .Zero_in(Zero),
    .RegWrite_in(u_ID_EX_Register_regwrite_out), .MemRead_in(u_ID_EX_Register_memread_out),
    .MemWrite_in(u_ID_EX_Register_memwrite_out), .MemToReg_in(u_ID_EX_Register_memtoreg_out),
    .Branch_in(u_ID_EX_Register_branch_out), .Jump_in(u_ID_EX_Register_jump_out),
    .ALUResult_out(MEM_ALUResult), .rd_out(u_EX_MEM_Register_rd_out),
    .RegWrite_out(u_EX_MEM_Register_regwrite_out), .MemToReg_out(u_EX_MEM_Register_memtoreg_out));  // open: PC_out, WriteData_out, Zero_out, MemRead_out, MemWrite_out, Branch_out, Jump_out
  InstructionDecoder_32 #(.applicationType("IVERILOG"), .CodeFile("/Users/kellysoares/Documents/Faculdade/arqComp/RICV_entrega/InstructionDecoder_32.v")) u_InstructionDecoder_32 (
    .Instruction(IF_ID_Instruction), .opcode(ID_opcode), .rs1(ID_rs1), .rs2(ID_rs2), .rd(ID_rd),
    .funct3(ID_funct3), .funct7(ID_funct7));
  ImmediateGenerator_32 #(.applicationType("IVERILOG"), .CodeFile("/Users/kellysoares/Documents/Faculdade/arqComp/RICV_entrega/ImmediateGenerator_32.v")) u_ImmediateGenerator_32 (
    .Instruction(IF_ID_Instruction), .Immediate(ID_Immediate));
  MEM_WB_Register #(.applicationType("IVERILOG"), .CodeFile("/Users/kellysoares/Documents/Faculdade/arqComp/RICV_entrega/MEM_WB_Register.v")) u_MEM_WB_Register (
    .clk(clk), .reset(reset), .Flush(MEM_WB_Flush), .ALUResult_in(MEM_ALUResult),
    .ReadData_in(MEM_ReadData_Temp), .rd_in(u_EX_MEM_Register_rd_out),
    .RegWrite_in(u_EX_MEM_Register_regwrite_out), .MemToReg_in(u_EX_MEM_Register_memtoreg_out),
    .ALUResult_out(WB_ALUResult));  // open: ReadData_out, rd_out, RegWrite_out, MemToReg_out
  ControlUnit_32 #(.applicationType("IVERILOG"), .CodeFile("/Users/kellysoares/Documents/Faculdade/arqComp/RICV_entrega/ControlUnit_32.v")) u_ControlUnit_32 (
    .opcode(ID_opcode), .RegWrite(ID_RegWrite), .ALUSrc(ID_ALUSrc), .MemRead(ID_MemRead),
    .MemWrite(ID_MemWrite), .MemToReg(ID_MemToReg), .Branch(ID_Branch), .Jump(ID_Jump), .ALUOp(ID_ALUOp));
  ALUControl_32 #(.applicationType("IVERILOG"), .CodeFile("/Users/kellysoares/Documents/Faculdade/arqComp/RICV_entrega/ALUControl_32.v")) u_ALUControl_32 (
    .ALUOp(ID_ALUOp), .opcode(ID_opcode), .funct3(ID_funct3), .funct7(ID_funct7), .ALUControl(ID_ALUControl));
endmodule
